// Logisim project FPU-prototyping.circ as structural Verilog
module CPU (
  input  clock,
  input  [31:0] in_2,
  input  [31:0] in_3,
  input  reset,
  output [31:0] out_5,
  output [31:0] out_6
);

  wire and_1_out, undriven_2, undriven_3, undriven_5;
  wire [2:0] alu_1_condition;
  wire [4:0] undriven_6;
  wire [31:0] alu_1_out_4, multiplexer_1_out, multiplexer_2_out, register_file_1_out_7,
       register_file_1_out_8, undriven, undriven_4;

  Multiplexer #(.width(32), .enable("false")) multiplexer_1 (
    .in0(alu_1_out_4), .in1(undriven), .out(multiplexer_1_out), .sel(undriven_2));
  and and_1 (and_1_out, clock, undriven_3);
  Register_File register_file_1 (
    .reset(reset), .in_2(multiplexer_1_out), .clock(and_1_out), .out_7(register_file_1_out_7),
    .out_8(register_file_1_out_8));  // open: address_rs1, address_rs2, address_rd
  Multiplexer #(.width(32), .enable("false")) multiplexer_2 (
    .in0(register_file_1_out_8), .in1(undriven_4), .out(multiplexer_2_out), .sel(undriven_5));
  ALU alu_1 (
    .\function (undriven_6), .in_2(register_file_1_out_7), .in_3(multiplexer_2_out), .out_4(alu_1_out_4),
    .condition(alu_1_condition));

  // Notes on the sheet:
  //   Instruction
  //   in Memory
  //   out Memory
  //   address Memory
endmodule

module Register_File (
  input  clock,
  input  [31:0] in_2,
  input  [3:0] address_rs1,
  input  [3:0] address_rs2,
  input  [3:0] address_rd,
  input  reset,
  output [31:0] out_7,
  output [31:0] out_8
);

  wire demultiplexer_2_out0, demultiplexer_2_out1, demultiplexer_2_out2, demultiplexer_2_out3,
       demultiplexer_2_out4, demultiplexer_2_out5, demultiplexer_2_out6, demultiplexer_2_out7,
       demultiplexer_2_out8, demultiplexer_2_out9, demultiplexer_2_out10, demultiplexer_2_out11,
       demultiplexer_2_out12, demultiplexer_2_out13, demultiplexer_2_out14, demultiplexer_2_out15;
  wire [31:0] demultiplexer_1_out0, demultiplexer_1_out1, demultiplexer_1_out2, demultiplexer_1_out3,
       demultiplexer_1_out4, demultiplexer_1_out5, demultiplexer_1_out6, demultiplexer_1_out7,
       demultiplexer_1_out8, demultiplexer_1_out9, demultiplexer_1_out10, demultiplexer_1_out11,
       demultiplexer_1_out12, demultiplexer_1_out13, demultiplexer_1_out14, demultiplexer_1_out15,
       register_1_q, register_2_q, register_3_q, register_4_q, register_5_q, register_6_q, register_7_q,
       register_8_q, register_9_q, register_10_q, register_11_q, register_12_q, register_13_q, register_14_q,
       register_15_q, register_16_q;

  Demultiplexer #(.select(4), .width(32), .enable("false")) demultiplexer_1 (
    .out0(demultiplexer_1_out0), .out1(demultiplexer_1_out1), .out2(demultiplexer_1_out2),
    .out3(demultiplexer_1_out3), .out4(demultiplexer_1_out4), .out5(demultiplexer_1_out5),
    .out6(demultiplexer_1_out6), .out7(demultiplexer_1_out7), .out8(demultiplexer_1_out8),
    .out9(demultiplexer_1_out9), .out10(demultiplexer_1_out10), .out11(demultiplexer_1_out11),
    .out12(demultiplexer_1_out12), .out13(demultiplexer_1_out13), .out14(demultiplexer_1_out14),
    .out15(demultiplexer_1_out15), .in(in_2), .sel(address_rd));
  Demultiplexer #(.select(4), .enable("false")) demultiplexer_2 (
    .out0(demultiplexer_2_out0), .out1(demultiplexer_2_out1), .out2(demultiplexer_2_out2),
    .out3(demultiplexer_2_out3), .out4(demultiplexer_2_out4), .out5(demultiplexer_2_out5),
    .out6(demultiplexer_2_out6), .out7(demultiplexer_2_out7), .out8(demultiplexer_2_out8),
    .out9(demultiplexer_2_out9), .out10(demultiplexer_2_out10), .out11(demultiplexer_2_out11),
    .out12(demultiplexer_2_out12), .out13(demultiplexer_2_out13), .out14(demultiplexer_2_out14),
    .out15(demultiplexer_2_out15), .in(clock), .sel(address_rd));
  Register #(.width(32), .trigger("falling")) register_1 (
    .D(demultiplexer_1_out0), .Q(register_1_q), .clk(demultiplexer_2_out0), .clr(reset));  // open: en
  Register #(.width(32)) register_2 (
    .D(demultiplexer_1_out1), .Q(register_2_q), .clk(demultiplexer_2_out1), .clr(reset));  // open: en
  Register #(.width(32)) register_3 (
    .D(demultiplexer_1_out2), .Q(register_3_q), .clk(demultiplexer_2_out2), .clr(reset));  // open: en
  Register #(.width(32)) register_4 (
    .D(demultiplexer_1_out3), .Q(register_4_q), .clk(demultiplexer_2_out3), .clr(reset));  // open: en
  Register #(.width(32)) register_5 (
    .D(demultiplexer_1_out4), .Q(register_5_q), .clk(demultiplexer_2_out4), .clr(reset));  // open: en
  Register #(.width(32)) register_6 (
    .D(demultiplexer_1_out5), .Q(register_6_q), .clk(demultiplexer_2_out5), .clr(reset));  // open: en
  Register #(.width(32)) register_7 (
    .D(demultiplexer_1_out6), .Q(register_7_q), .clk(demultiplexer_2_out6), .clr(reset));  // open: en
  Register #(.width(32)) register_8 (
    .D(demultiplexer_1_out7), .Q(register_8_q), .clk(demultiplexer_2_out7), .clr(reset));  // open: en
  Register #(.width(32)) register_9 (
    .D(demultiplexer_1_out8), .Q(register_9_q), .clk(demultiplexer_2_out8), .clr(reset));  // open: en
  Register #(.width(32)) register_10 (
    .D(demultiplexer_1_out9), .Q(register_10_q), .clk(demultiplexer_2_out9), .clr(reset));  // open: en
  Register #(.width(32)) register_11 (
    .D(demultiplexer_1_out10), .Q(register_11_q), .clk(demultiplexer_2_out10), .clr(reset));  // open: en
  Register #(.width(32)) register_12 (
    .D(demultiplexer_1_out11), .Q(register_12_q), .clk(demultiplexer_2_out11), .clr(reset));  // open: en
  Register #(.width(32)) register_13 (
    .D(demultiplexer_1_out12), .Q(register_13_q), .clk(demultiplexer_2_out12), .clr(reset));  // open: en
  Register #(.width(32)) register_14 (
    .D(demultiplexer_1_out13), .Q(register_14_q), .clk(demultiplexer_2_out13), .clr(reset));  // open: en
  Register #(.width(32)) register_15 (
    .D(demultiplexer_1_out14), .Q(register_15_q), .clk(demultiplexer_2_out14), .clr(reset));  // open: en
  Register #(.width(32)) register_16 (
    .D(demultiplexer_1_out15), .Q(register_16_q), .clk(demultiplexer_2_out15), .clr(reset));  // open: en
  Multiplexer #(.select(4), .width(32), .enable("false")) multiplexer_1 (
    .in0(register_1_q), .in1(register_2_q), .in2(register_3_q), .in3(register_4_q), .in4(register_5_q),
    .in5(register_6_q), .in6(register_7_q), .in7(register_8_q), .in8(register_9_q), .in9(register_10_q),
    .in10(register_11_q), .in11(register_12_q), .in12(register_13_q), .in13(register_14_q),
    .in14(register_15_q), .in15(register_16_q), .out(out_7), .sel(address_rs1));
  Multiplexer #(.select(4), .width(32), .enable("false")) multiplexer_2 (
    .in0(register_1_q), .in1(register_2_q), .in2(register_3_q), .in3(register_4_q), .in4(register_5_q),
    .in5(register_6_q), .in6(register_7_q), .in7(register_8_q), .in8(register_9_q), .in9(register_10_q),
    .in10(register_11_q), .in11(register_12_q), .in12(register_13_q), .in13(register_14_q),
    .in14(register_15_q), .in15(register_16_q), .out(out_8), .sel(address_rs2));

  // Notes on the sheet:
  //   value in
  //   reg0
  //   reg15
  //   rs1 out
  //   rs2 out
  //   ex. rd = rs1 + rs2
  //   FADD rd, rs1, rs2
  //   rd = destination register
  //   rs1 = first operand/source
  //   rs2 = second operand/source
endmodule

module ALU (
  input  [4:0] \function ,
  input  [31:0] in_2,
  input  [31:0] in_3,
  output [31:0] out_4,
  output [2:0] condition
);

  Multiplexer #(.select(5), .width(32), .enable("false")) multiplexer_1 (
    .out(out_4), .sel(\function ));  // open: in0, in1, in2, in3, in4, in5, in6, in7, in8, in9, in10, in11, in12, in13, in14, in15, in16, in17, in18, in19, in20, in21, in22, in23, in24, in25, in26, in27, in28, in29, in30, in31

  // Notes on the sheet:
  //   x
  //   y
  //   out
  //   (Z, V, N)
endmodule

module c_type_decode (
  input  [31:0] in_1,
  output [3:0] rs2,
  output [3:0] rd,
  output [5:0] out_4,
  output [3:0] rs1
);


  assign out_4 = in_1[31:26];
  assign rd = in_1[25:22];
  assign rs1 = in_1[21:18];
  assign rs2 = in_1[17:14];

  // Notes on the sheet:
  //   instruction
  //   not used
  //   opcode
endmodule
